// Logisim project lab06partA.circ as structural Verilog: 1 circuit, main circuit main
module main (
  input  in_1,
  input  in_2,
  input  in_3,
  output out_4,
  output out_5
);

  wire A1_out, A2_out, A3_out, A4_out, A5_out, A6_out, A7_out, A8_out, A9_out, A10_out, A11_out, not_1_out,
       not_2_out, not_3_out, O1_2_out, O1_3_out, O1_out;

  not not_1 (not_1_out, in_1);
  not not_2 (not_2_out, in_2);
  not not_3 (not_3_out, in_3);
  and A1 (A1_out, not_1_out, not_2_out);
  and A3 (A3_out, not_1_out, in_2);
  and A5 (A5_out, in_1, not_2_out);
  and A7 (A7_out, in_1, in_2);
  and A9 (A9_out, in_3, in_1);
  buf A10 (A10_out, in_2);  // AND_Gate
  buf A11 (A11_out, in_2);  // AND_Gate
  and A2 (A2_out, A1_out, in_3);
  and A4 (A4_out, A3_out, not_3_out);
  and A6 (A6_out, A5_out, not_3_out);
  and A8 (A8_out, A7_out, in_3);
  or O1 (O1_out, A6_out, A8_out);
  or O1_2 (O1_2_out, A9_out, A10_out);
  or O1_3 (O1_3_out, A2_out, A4_out);
  or O1_4 (out_5, O1_2_out, A11_out);
  or O1_5 (out_4, O1_3_out, O1_out);
endmodule
