// Logisim project lab08.circ as structural Verilog: 3 circuits, main circuit main
module main (
  input  [3:0] in_1,
  input  [7:0] A,
  input  [7:0] B,
  output Zero,
  output [7:0] Result,
  output Overflow
);

  Fourbit_ALU _8bit_ALU (.operation(in_1), .A(A), .B(B), .Result(Result), .Zero(Zero), .Overflow(Overflow));

  // Notes on the sheet:
  //   0 = and
  //   1 = or
  //   10 = Addition
  //   11 = Less
endmodule

module One_bit_ALU (
  input  CIn,
  input  [1:0] Operation,
  input  Binvert,
  input  Ainvert,
  input  a,
  input  b,
  input  less,
  output Result,
  output Set,
  output CarryOut
);

  wire and_1_out, multiplexer_1_out, multiplexer_2_out, not_1_out, not_2_out, or_1_out;

  not not_1 (not_1_out, a);
  not not_2 (not_2_out, b);
  Multiplexer multiplexer_1 (.in0(a), .in1(not_1_out), .out(multiplexer_1_out), .sel(Ainvert));  // open: en
  Multiplexer multiplexer_2 (.in0(b), .in1(not_2_out), .out(multiplexer_2_out), .sel(Binvert));  // open: en
  and and_1 (and_1_out, multiplexer_1_out, multiplexer_2_out);
  or or_1 (or_1_out, multiplexer_1_out, multiplexer_2_out);
  Adder #(.width(1)) adder_1 (.a(multiplexer_1_out), .b(multiplexer_2_out), .out(Set), .cin(CIn), .cout(CarryOut));
  Multiplexer #(.select(2)) multiplexer_3 (
    .in0(and_1_out), .in1(or_1_out), .in2(Set), .in3(less), .out(Result), .sel(Operation));  // open: en
endmodule

module Fourbit_ALU (
  input  [3:0] operation,
  input  [7:0] A,
  input  [7:0] B,
  output [7:0] Result,
  output Zero,
  output Overflow
);

  wire one_bit_alu_1_carryout, one_bit_alu_2_carryout, one_bit_alu_3_carryout, one_bit_alu_4_carryout,
       one_bit_alu_5_carryout, one_bit_alu_6_carryout, one_bit_alu_7_carryout, one_bit_alu_8_set, or_1_out;

  One_bit_ALU one_bit_alu_1 (
    .CIn(operation[2]), .Operation(operation[1:0]), .Binvert(operation[2]), .Ainvert(operation[3]), .a(A[0]),
    .b(B[0]), .less(one_bit_alu_8_set), .Result(Result[0]), .CarryOut(one_bit_alu_1_carryout));  // open: Set
  One_bit_ALU one_bit_alu_2 (
    .CIn(one_bit_alu_1_carryout), .Operation(operation[1:0]), .Binvert(operation[2]), .Ainvert(operation[3]),
    .a(A[1]), .b(B[1]), .less(1'b0), .Result(Result[1]), .CarryOut(one_bit_alu_2_carryout));  // open: Set
  One_bit_ALU one_bit_alu_3 (
    .CIn(one_bit_alu_2_carryout), .Operation(operation[1:0]), .Binvert(operation[2]), .Ainvert(operation[3]),
    .a(A[2]), .b(B[2]), .less(1'b0), .Result(Result[2]), .CarryOut(one_bit_alu_3_carryout));  // open: Set
  One_bit_ALU one_bit_alu_4 (
    .CIn(one_bit_alu_3_carryout), .Operation(operation[1:0]), .Binvert(operation[2]), .Ainvert(operation[3]),
    .a(A[3]), .b(B[3]), .less(1'b0), .Result(Result[3]), .CarryOut(one_bit_alu_4_carryout));  // open: Set
  One_bit_ALU one_bit_alu_5 (
    .CIn(one_bit_alu_4_carryout), .Operation(operation[1:0]), .Binvert(operation[2]), .Ainvert(operation[3]),
    .a(A[4]), .b(B[4]), .less(1'b0), .Result(Result[4]), .CarryOut(one_bit_alu_5_carryout));  // open: Set
  One_bit_ALU one_bit_alu_6 (
    .CIn(one_bit_alu_5_carryout), .Operation(operation[1:0]), .Binvert(operation[2]), .Ainvert(operation[3]),
    .a(A[5]), .b(B[5]), .less(1'b0), .Result(Result[5]), .CarryOut(one_bit_alu_6_carryout));  // open: Set
  One_bit_ALU one_bit_alu_7 (
    .CIn(one_bit_alu_6_carryout), .Operation(operation[1:0]), .Binvert(operation[2]), .Ainvert(operation[3]),
    .a(A[6]), .b(B[6]), .less(1'b0), .Result(Result[6]), .CarryOut(one_bit_alu_7_carryout));  // open: Set
  One_bit_ALU one_bit_alu_8 (
    .CIn(one_bit_alu_7_carryout), .Operation(operation[1:0]), .Binvert(operation[2]), .Ainvert(operation[3]),
    .a(A[7]), .b(B[7]), .less(1'b0), .Result(Result[7]), .Set(one_bit_alu_8_set), .CarryOut(Overflow));
  or or_1 (or_1_out, Result[0], Result[1], Result[2], Result[3], Result[4], Result[5], Result[6], Result[7]);
  not not_1 (Zero, or_1_out);
endmodule
