// Logisim project lab09.circ as structural Verilog: 2 circuits, main circuit main
module main (
  input  [7:0] Multiplier,
  input  [7:0] Multiplicand,
  output [15:0] Product
);

  _4_bit_Multiplier u_4_bit_multiplier_1 (.Multiplier(Multiplier), .Multiplicand(Multiplicand), .Product(Product));

  // Notes on the sheet:
  //   Use 8 bit input and 16 bit output if we doing 8 bit multiplier
endmodule

module _4_bit_Multiplier (
  input  [7:0] Multiplier,
  input  [7:0] Multiplicand,
  output [15:0] Product
);

  wire [15:0] adder_1_out, adder_2_out, adder_3_out, adder_4_out, adder_5_out, adder_6_out, adder_7_out,
       adder_8_out, multiplexer_1_out, multiplexer_2_out, multiplexer_3_out, multiplexer_4_out,
       multiplexer_5_out, multiplexer_6_out, multiplexer_7_out, shifter_1_out, shifter_2_out, shifter_3_out,
       shifter_4_out, shifter_5_out, shifter_6_out, shifter_7_out;

  Adder #(.width(16)) adder_1 (.a({16{1'b0}}), .b({{8{1'b0}}, Multiplicand}), .out(adder_1_out));  // open: cin, cout
  Multiplexer #(.width(16)) multiplexer_1 (
    .in0({16{1'b0}}), .in1(adder_1_out), .out(multiplexer_1_out), .sel(Multiplier[0]));  // open: en
  Shifter #(.width(16)) shifter_1 (.in({{8{1'b0}}, Multiplicand}), .\dist (4'b0001), .out(shifter_1_out));
  Adder #(.width(16)) adder_2 (.a(multiplexer_1_out), .b(shifter_1_out), .out(adder_2_out));  // open: cin, cout
  Multiplexer #(.width(16)) multiplexer_2 (
    .in0(multiplexer_1_out), .in1(adder_2_out), .out(multiplexer_2_out), .sel(Multiplier[1]));  // open: en
  Shifter #(.width(16)) shifter_2 (.in(shifter_1_out), .\dist (4'b0001), .out(shifter_2_out));
  Adder #(.width(16)) adder_3 (.a(multiplexer_2_out), .b(shifter_2_out), .out(adder_3_out));  // open: cin, cout
  Multiplexer #(.width(16)) multiplexer_3 (
    .in0(multiplexer_2_out), .in1(adder_3_out), .out(multiplexer_3_out), .sel(Multiplier[2]));  // open: en
  Shifter #(.width(16)) shifter_3 (.in(shifter_2_out), .\dist (4'b0001), .out(shifter_3_out));
  Multiplexer #(.width(16)) multiplexer_4 (
    .in0(multiplexer_3_out), .in1(adder_4_out), .out(multiplexer_4_out), .sel(Multiplier[3]));  // open: en
  Adder #(.width(16)) adder_4 (.a(multiplexer_3_out), .b(shifter_3_out), .out(adder_4_out));  // open: cin, cout
  Shifter #(.width(16)) shifter_4 (.in(shifter_3_out), .\dist (4'b0001), .out(shifter_4_out));
  Adder #(.width(16)) adder_5 (.a(multiplexer_4_out), .b(shifter_4_out), .out(adder_5_out));  // open: cin, cout
  Multiplexer #(.width(16)) multiplexer_5 (
    .in0(multiplexer_4_out), .in1(adder_5_out), .out(multiplexer_5_out), .sel(Multiplier[4]));  // open: en
  Shifter #(.width(16)) shifter_5 (.in(shifter_4_out), .\dist (4'b0001), .out(shifter_5_out));
  Adder #(.width(16)) adder_6 (.a(multiplexer_5_out), .b(shifter_5_out), .out(adder_6_out));  // open: cin, cout
  Multiplexer #(.width(16)) multiplexer_6 (
    .in0(multiplexer_5_out), .in1(adder_6_out), .out(multiplexer_6_out), .sel(Multiplier[5]));  // open: en
  Shifter #(.width(16)) shifter_6 (.in(shifter_5_out), .\dist (4'b0001), .out(shifter_6_out));
  Multiplexer #(.width(16)) multiplexer_7 (
    .in0(multiplexer_6_out), .in1(adder_7_out), .out(multiplexer_7_out), .sel(Multiplier[6]));  // open: en
  Adder #(.width(16)) adder_7 (.a(multiplexer_6_out), .b(shifter_6_out), .out(adder_7_out));  // open: cin, cout
  Shifter #(.width(16)) shifter_7 (.in(shifter_6_out), .\dist (4'b0001), .out(shifter_7_out));
  Adder #(.width(16)) adder_8 (.a(multiplexer_7_out), .b(shifter_7_out), .out(adder_8_out));  // open: cin, cout
  Multiplexer #(.width(16)) multiplexer_8 (
    .in0(multiplexer_7_out), .in1(adder_8_out), .out(Product), .sel(Multiplier[7]));  // open: en
endmodule
