// Logisim project lab10.circ as structural Verilog: 1 circuit, main circuit main
module main (
  input  WriteEnable,
  input  [2:0] ReadRegister1,
  input  [2:0] ReadRegister2,
  input  [2:0] WriteRegister,
  input  [31:0] WriteData,
  output [31:0] ReadData1,
  output [31:0] ReadData2
);

  wire clock_out, demultiplexer_1_out0, demultiplexer_1_out1, demultiplexer_1_out2, demultiplexer_1_out3,
       demultiplexer_1_out4, demultiplexer_1_out5, demultiplexer_1_out6, demultiplexer_1_out7;
  wire [31:0] register_1_q, register_2_q, register_3_q, register_4_q, register_5_q, register_6_q,
       register_7_q, register_8_q;

  Demultiplexer #(.select(3)) demultiplexer_1 (
    .out0(demultiplexer_1_out0), .out1(demultiplexer_1_out1), .out2(demultiplexer_1_out2),
    .out3(demultiplexer_1_out3), .out4(demultiplexer_1_out4), .out5(demultiplexer_1_out5),
    .out6(demultiplexer_1_out6), .out7(demultiplexer_1_out7), .in(WriteEnable), .sel(WriteRegister));  // open: en
  Clock clock (.out(clock_out));
  Register #(.width(32)) register_1 (
    .D(WriteData), .en(demultiplexer_1_out0), .Q(register_1_q), .clk(clock_out));  // open: clr
  Register #(.width(32)) register_2 (
    .D(WriteData), .en(demultiplexer_1_out1), .Q(register_2_q), .clk(clock_out));  // open: clr
  Register #(.width(32)) register_3 (
    .D(WriteData), .en(demultiplexer_1_out2), .Q(register_3_q), .clk(clock_out));  // open: clr
  Register #(.width(32)) register_4 (
    .D(WriteData), .en(demultiplexer_1_out3), .Q(register_4_q), .clk(clock_out));  // open: clr
  Register #(.width(32)) register_5 (
    .D(WriteData), .en(demultiplexer_1_out4), .Q(register_5_q), .clk(clock_out));  // open: clr
  Register #(.width(32)) register_6 (
    .D(WriteData), .en(demultiplexer_1_out5), .Q(register_6_q), .clk(clock_out));  // open: clr
  Register #(.width(32)) register_7 (
    .D(WriteData), .en(demultiplexer_1_out6), .Q(register_7_q), .clk(clock_out));  // open: clr
  Register #(.width(32)) register_8 (
    .D(WriteData), .en(demultiplexer_1_out7), .Q(register_8_q), .clk(clock_out));  // open: clr
  Multiplexer #(.select(3), .width(32)) multiplexer_1 (
    .in0(register_1_q), .in1(register_2_q), .in2(register_3_q), .in3(register_4_q), .in4(register_5_q),
    .in5(register_6_q), .in6(register_7_q), .in7(register_8_q), .out(ReadData1), .sel(ReadRegister1));  // open: en
  Multiplexer #(.select(3), .width(32)) multiplexer_2 (
    .in0(register_1_q), .in1(register_2_q), .in2(register_3_q), .in3(register_4_q), .in4(register_5_q),
    .in5(register_6_q), .in6(register_7_q), .in7(register_8_q), .out(ReadData2), .sel(ReadRegister2));  // open: en
endmodule
