// Logisim project lab10practice.circ as structural Verilog: 1 circuit, main circuit main
module main (
  input  ReadRegister,
  input  WriteEnable,
  input  WriteRegister,
  input  [7:0] WriteData,
  output [7:0] out_5
);

  wire clock_1_out, demultiplexer_1_out0, demultiplexer_1_out1;
  wire [7:0] register_1_q, register_2_q;

  Demultiplexer demultiplexer_1 (
    .out0(demultiplexer_1_out0), .out1(demultiplexer_1_out1), .in(WriteEnable), .sel(WriteRegister));  // open: en
  Clock clock_1 (.out(clock_1_out));
  Register register_1 (.D(WriteData), .en(demultiplexer_1_out0), .Q(register_1_q), .clk(clock_1_out));  // open: clr
  Register register_2 (.D(WriteData), .en(demultiplexer_1_out1), .Q(register_2_q), .clk(clock_1_out));  // open: clr
  Multiplexer #(.width(8)) multiplexer_1 (
    .in0(register_1_q), .in1(register_2_q), .out(out_5), .sel(ReadRegister));  // open: en
endmodule
