// Logisim project lab11.circ as structural Verilog: 1 circuit, main circuit main
module main (
  input  Write,
  input  in_2,
  input  Clear
);

  wire clock_1_out, counter_1_carry, counter_3_carry, not_1_out, not_2_out, Reset_2_out, Reset_out;
  wire [3:0] counter_2_q, counter_3_q, ram_1_data;

  Counter #(.width(4), .max('h0), .ongoal("stay")) counter_1 (
    .carry(counter_1_carry), .clk(clock_1_out), .clr(Reset_out));  // open: load, D, count, Q
  Clock clock_1 (.out(clock_1_out));
  not not_1 (not_1_out, counter_1_carry);
  Counter #(.width(4), .max('hf), .ongoal("stay")) counter_2 (
    .load(not_1_out), .Q(counter_2_q), .clk(clock_1_out), .clr(Reset_out));  // open: D, count, carry
  Button Reset (.out(Reset_out));
  RAM #(.addrWidth(4), .dataWidth(4)) ram_1 (
    .addr(counter_2_q), .data(ram_1_data), .sel(Write), .clk(clock_1_out), .ld(in_2), .clr(Clear));
  Button Reset_2 (.out(Reset_2_out));
  assign ram_1_data = not_2_out ? counter_3_q : 4'bz;  // Controlled_Buffer controlled_buffer_1
  not not_2 (not_2_out, counter_3_carry);
  Counter #(.width(4), .max('hf), .ongoal("stay")) counter_3 (
    .Q(counter_3_q), .carry(counter_3_carry), .clk(clock_1_out), .clr(Reset_2_out));  // open: load, D, count
endmodule
