// Logisim project lab12.circ as structural Verilog: 4 circuits, main circuit main
module main (
);

  wire button_1_out, clock_1_out, decoder_3_destmux0, fields_1_dest, not_1_out;
  wire [1:0] decoder_3_alu;
  wire [3:0] fields_1_opcode;
  wire [7:0] A_q, adder_1_out, alu_1_output, B_q, fields_1_imm8, multiplexer_2_out, register_1_q;
  wire [15:0] rom_1_data;

  Multiplexer multiplexer_1 ();  // open: in0, in1, out, sel, en
  Decoder_part decoder_1 ();  // open: out0, out1, sel, en
  Adder adder_1 (.a(register_1_q), .b(8'h1), .out(adder_1_out));  // open: cin, cout
  Clock clock_1 (.out(clock_1_out));
  Button button_1 (.out(button_1_out));
  Register register_1 (.D(adder_1_out), .Q(register_1_q), .clk(clock_1_out), .clr(button_1_out));  // open: en
  Decoder decoder_2 ();  // open: opcode, ALU, DestMUX0
  Counter counter_1 ();  // open: load, D, count, Q, carry, clk, clr
  Fields fields_1 (.instruction(rom_1_data), .imm8(fields_1_imm8), .Dest(fields_1_dest), .opcode(fields_1_opcode));
  ROM #(.dataWidth(16)) rom_1 (.addr(register_1_q), .data(rom_1_data), .sel(1'b1));
  Fields fields_2 ();  // open: instruction, imm8, Dest, opcode
  not not_1 (not_1_out, fields_1_dest);
  Decoder decoder_3 (.opcode(fields_1_opcode), .ALU(decoder_3_alu), .DestMUX0(decoder_3_destmux0));
  Decoder decoder_4 ();  // open: opcode, ALU, DestMUX0
  Register A (.D(multiplexer_2_out), .en(not_1_out), .Q(A_q), .clk(clock_1_out));  // open: clr
  Register B (.D(multiplexer_2_out), .en(fields_1_dest), .Q(B_q), .clk(clock_1_out));  // open: clr
  ALU alu_1 (.A(A_q), .B(B_q), .opcode(decoder_3_alu), .\output (alu_1_output));
  Multiplexer #(.width(8)) multiplexer_2 (
    .in0(alu_1_output), .in1(fields_1_imm8), .out(multiplexer_2_out), .sel(decoder_3_destmux0));  // open: en

  // Notes on the sheet:
  //   contents of rom_1 (hex, n*v repeats v):
  //   1 802 105 804
endmodule

module ALU (
  input  [7:0] A,
  input  [7:0] B,
  input  [1:0] opcode,
  output [7:0] \output 
);

  wire [7:0] adder_1_out, and_1_out, or_1_out, subtractor_1_out;

  Adder adder_1 (.a(A), .b(B), .out(adder_1_out));  // open: cin, cout
  Subtractor subtractor_1 (.a(A), .b(B), .out(subtractor_1_out));  // open: bin, bout
  assign or_1_out = A | B;  // OR_Gate or_1, 8 bits wide
  assign and_1_out = A & B;  // AND_Gate and_1, 8 bits wide
  Multiplexer #(.select(2), .width(8)) multiplexer_1 (
    .in0(adder_1_out), .in1(subtractor_1_out), .in2(or_1_out), .in3(and_1_out), .out(\output ), .sel(opcode));  // open: en
endmodule

module Fields (
  input  [15:0] instruction,
  output [7:0] imm8,
  output Dest,
  output [3:0] opcode
);


  assign Dest = instruction[11];
  assign imm8 = instruction[7:0];
  assign opcode = instruction[15:12];
endmodule

module Decoder (
  input  [3:0] opcode,
  output [1:0] ALU,
  output DestMUX0
);

  wire not_2_out, not_3_out;

  not not_1 (ALU[1], opcode[1]);
  not not_2 (not_2_out, opcode[2]);
  not not_3 (not_3_out, opcode[1]);
  and and_1 (DestMUX0, not_2_out, not_3_out);

  assign ALU[0] = opcode[0];
endmodule
